# Fritzing sketch V1 (saved by Fritzing 0.9.4)

parts:
  U1 = NodeMCU V1.0
  LED1 = RGB LED (com. cathode, rgb) [package="5 mm [THT]"]
  OLED1 = OLED Mono 0.56 inch blue or white

nets:
  N1: U1.D1, OLED1.SCL
  N2: U1.D2, OLED1.SDA
  3V3: U1.3V3, OLED1.VCC
  N3: U1.GND, LED1.common_cathode
  N4: U1.D5, LED1.red_anode
  N5: U1.D6, LED1.green_anode
  N6: U1.D7, LED1.blue_anode

custom parts:
  NodeMCU V1.0: ESP8266 based NodeMCU
  OLED Mono 0.56 inch blue or white: OLED, I2C 3.3V - 5V Blue and White text versions
